// Logisim project Ripple_Counter.circ as structural Verilog: 1 circuit, main circuit main
module main (
  input  RESET,
  output Out3,
  output Out2,
  output Out1,
  output Out0
);

  wire CLK_out, Q0_qn, Q1_qn, Q2_qn, Q3_qn;

  Clock CLK (.out(CLK_out));
  D_Flip_Flop Q0 (.clk(CLK_out), .D(Q0_qn), .Q(Out0), .Qn(Q0_qn), .reset(RESET));  // open: preset
  D_Flip_Flop Q1 (.clk(Q0_qn), .D(Q1_qn), .Q(Out1), .Qn(Q1_qn), .reset(RESET));  // open: preset
  D_Flip_Flop Q2 (.clk(Q1_qn), .D(Q2_qn), .Q(Out2), .Qn(Q2_qn), .reset(RESET));  // open: preset
  D_Flip_Flop Q3 (.clk(Q2_qn), .D(Q3_qn), .Q(Out3), .Qn(Q3_qn), .reset(RESET));  // open: preset
endmodule
